// Logisim project Envases.circ as structural Verilog: 3 circuits, main circuit main
module main (
  input  RST,
  input  CLK,
  input  I,
  input  L,
  input  G,
  input  R,
  input  E,
  input  S,
  output LL,
  output out_10,
  output SL,
  output out_12,
  output out_13,
  output out_14,
  output INS,
  output out_16
);

  wire Q;

  Proceso_Moore proceso_moore_1 (
    .RST(RST), .CLK(CLK), .L(L), .F(out_10), .E(E), .S(S), .LL(LL), .SL(SL), .Q(Q), .INS(INS));
  Clasificacion_Mealy clasificacion_mealy_1 (
    .Q(Q), .I(I), .CLK(CLK), .G(G), .R(R), .RST(RST), .F(out_10), .DV(out_12), .ERR(out_13), .OK(out_14),
    .AV(out_16));

  // Other names for the same wires on the sheet: F = out_10
endmodule

module Proceso_Moore (
  input  RST,
  input  CLK,
  input  L,
  input  F,
  input  E,
  input  S,
  output LL,
  output SL,
  output Q,
  output INS
);

  wire D_p0_out, D_p1_out, not_1_out, not_2_out, not_3_out, P0_E_out, p0_next_out, p0_q, p0_qn, P1_L_out,
       p1_next_out, P1_nL_out, p1_q, p1_qn, P2_S_out, P3_nF_out, PO_out;

  D_Flip_Flop p1 (.D(D_p1_out), .clk(CLK), .Q(p1_q), .Qn(p1_qn));  // open: preset, reset
  D_Flip_Flop p0 (.D(D_p0_out), .clk(CLK), .Q(p0_q), .Qn(p0_qn));  // open: preset, reset
  and PO (PO_out, p1_qn, p0_qn);
  and PI (LL, p1_qn, p0_q);
  and P2 (SL, p1_q, p0_qn);
  and P3 (INS, p1_q, p0_q);
  not not_1 (not_1_out, F);
  and P1_nL (P1_nL_out, LL, not_2_out);
  not not_2 (not_2_out, L);
  and P2_S (P2_S_out, SL, S);
  and P1_L (P1_L_out, L, LL);
  and P3_nF (P3_nF_out, not_1_out, INS);
  and P0_E (P0_E_out, PO_out, E);
  or p1_next (p1_next_out, P1_L_out, SL, P3_nF_out);
  not not_3 (not_3_out, RST);
  or p0_next (p0_next_out, P0_E_out, P1_nL_out, P2_S_out, P3_nF_out);
  and D_p1 (D_p1_out, not_3_out, p1_next_out);
  and D_p0 (D_p0_out, not_3_out, p0_next_out);

  assign Q = INS;
endmodule

module Clasificacion_Mealy (
  input  Q,
  input  I,
  input  CLK,
  input  G,
  input  R,
  input  RST,
  output F,
  output DV,
  output ERR,
  output OK,
  output AV
);

  wire b0_next_out, b0_q, B0_Q_I_G_out, B0_Q_I_nG_out, b0_qn, b1_next_out, B1_or_B2, b1_q, b1_qn, B2_R_out,
       B3_out, B3_Q_out, BI, BO_out, D_b0_out, D_b1_out, not_1_out, not_2_out, Rn;

  D_Flip_Flop b1 (.D(D_b1_out), .clk(CLK), .Q(b1_q), .Qn(b1_qn));  // open: preset, reset
  D_Flip_Flop b0 (.D(D_b0_out), .clk(CLK), .Q(b0_q), .Qn(b0_qn));  // open: preset, reset
  and BO (BO_out, b1_qn, b0_qn);
  and u_BI (BI, b1_qn, b0_q);
  and B2 (ERR, b0_qn, b1_q);
  and B3 (B3_out, b1_q, b0_q);
  and B0_Q_I_nG (B0_Q_I_nG_out, BO_out, Q, I, not_1_out);
  and B1_R (OK, BI, R);
  and B3_Q (B3_Q_out, Q, B3_out);
  and B2_R (B2_R_out, ERR, R);
  and B0_Q_I_G (B0_Q_I_G_out, BO_out, Q, I, G);
  and DV_logic (DV, ERR, Rn);
  or u_B1_or_B2 (B1_or_B2, ERR, BI);
  not not_1 (not_1_out, G);
  not not_2 (not_2_out, RST);
  or b1_next (b1_next_out, B0_Q_I_nG_out, OK, B3_Q_out, ERR);
  or b0_next (b0_next_out, B2_R_out, BI, B3_Q_out, B0_Q_I_G_out);
  and F_logic (F, B1_or_B2, R);
  and AV_logic (AV, B1_or_B2, Rn);
  not not_3 (Rn, R);
  and D_b1 (D_b1_out, not_2_out, b1_next_out);
  and D_b0 (D_b0_out, not_2_out, b0_next_out);

  // Other names for the same wires on the sheet: B1_R = OK; B2 = ERR
endmodule
